# Fritzing sketch 4Channel_Relay_Arduino (saved by Fritzing 0.9.3b)
breadboards: 1

parts:
  Part1 = Arduino Uno (Rev3)
  S1 = Square Pushbutton
  S2 = Square Pushbutton
  S3 = Square Pushbutton
  S4 = Square Pushbutton
  LED2 = LED - 5mm [color="Red (633nm)" package="5 mm [THT]"]
  LED3 = LED - 5mm [color="Red (633nm)" package="5 mm [THT]"]
  LED4 = LED - 5mm [color="Red (633nm)" package="5 mm [THT]"]
  LED5 = LED - 5mm [color="Red (633nm)" package="5 mm [THT]"]
  R1 = Resistor [tolerance=±5% resistance=220 package="0805 [SMD]"]  # not connected
  R3 = Resistor [tolerance=±5% resistance=220 package="0805 [SMD]"]
  R4 = Resistor [tolerance=±5% resistance=220 package="0805 [SMD]"]
  R5 = Resistor [tolerance=±5% resistance=220 package="0805 [SMD]"]

nets:
  N1: Part1.A2, S1.leg0, LED5.cathode
  N2: Part1.A3, S4.leg0, LED4.cathode
  N3: Part1.A4/SDA, S3.leg0, LED3.cathode
  N4: Part1.A5/SCL, S2.leg0, LED2.cathode
  N5: Part1.5V, R3.Pin_1, R4.Pin_1, R5.Pin_1
  N6: Part1.GND, S1.leg1, S2.leg1, S3.leg1, S4.leg1
  N7: LED3.anode, R5.Pin_0
  N8: LED4.anode, R3.Pin_0
  N9: LED5.anode, R4.Pin_0

notes:
  This is the 4 channel Relay. 4 inputs and then a VCC and GRN
